// Logisim project AluReg.circ as structural Verilog: 6 circuits, main circuit 1_3-Estados-1bit
module _1_3_Estados_1bit (
  input  A,
  input  A_en,
  input  B,
  input  B_en,
  input  C,
  input  C_en,
  output Res
);

  assign Res = A_en ? A : 1'bz;  // Controlled_Buffer controlled_buffer_1
  assign Res = B_en ? B : 1'bz;  // Controlled_Buffer controlled_buffer_2
  assign Res = C_en ? C : 1'bz;  // Controlled_Buffer controlled_buffer_3

  // Notes on the sheet:
  //   1) Componentes de 3 Estado - Bus de Salida
  //   Nro de Grupo: 28
endmodule

module _2a_Reg_Salida_Restringida_1bit (
  input  clck,
  input  in,
  input  w,
  input  en_out,
  output out_debug,
  output out
);

  D_Flip_Flop d_ff_1 (.clk(clck), .D(in), .Q(out_debug), .en(w));  // open: Qn, preset, reset
  assign out = en_out ? out_debug : 1'bz;  // Controlled_Buffer controlled_buffer_1

  // Notes on the sheet:
  //   2a) Registro de Salida Restringida - 1 bit
  //   Nro de Grupo: 28
endmodule

module _2b_Transferencia_Registros (
  input  W_0,
  input  en_0,
  input  W_1,
  input  en_1,
  input  W_2,
  input  en_2,
  input  force_input,
  input  en_force_input,
  output R0,
  output BUS,
  output R1,
  output R2
);

  wire clock_1_out;

  Clock clock_1 (.out(clock_1_out));
  assign BUS = en_force_input ? force_input : 1'bz;  // Controlled_Buffer controlled_buffer_1
  _2a_Reg_Salida_Restringida_1bit u_2a_reg_salida_restringida_1bit_1 (
    .in(BUS), .out_debug(R0), .out(BUS), .w(W_0), .en_out(en_0), .clck(clock_1_out));
  _2a_Reg_Salida_Restringida_1bit u_2a_reg_salida_restringida_1bit_2 (
    .in(BUS), .out_debug(R1), .out(BUS), .w(W_1), .en_out(en_1), .clck(clock_1_out));
  _2a_Reg_Salida_Restringida_1bit u_2a_reg_salida_restringida_1bit_3 (
    .in(BUS), .out_debug(R2), .out(BUS), .w(W_2), .en_out(en_2), .clck(clock_1_out));

  // Notes on the sheet:
  //   2b) Secuencia de Transferencia entre Registros - 1 bit
  //   Nro de Grupo: 28
endmodule

module _3a_Reg_Salida_Restringida_4bits (
  input  [3:0] In_4,
  input  en_out,
  input  w,
  input  clk,
  output [3:0] out4_d,
  output [3:0] out
);

  _2a_Reg_Salida_Restringida_1bit u_2a_reg_salida_restringida_1bit_1 (
    .in(In_4[0]), .out(out4_d[0]), .w(w), .en_out(1'b1), .clck(clk));  // open: out_debug
  _2a_Reg_Salida_Restringida_1bit u_2a_reg_salida_restringida_1bit_2 (
    .in(In_4[1]), .out(out4_d[1]), .w(w), .en_out(1'b1), .clck(clk));  // open: out_debug
  _2a_Reg_Salida_Restringida_1bit u_2a_reg_salida_restringida_1bit_3 (
    .in(In_4[2]), .out(out4_d[2]), .w(w), .en_out(1'b1), .clck(clk));  // open: out_debug
  _2a_Reg_Salida_Restringida_1bit u_2a_reg_salida_restringida_1bit_4 (
    .in(In_4[3]), .out(out4_d[3]), .w(w), .en_out(1'b1), .clck(clk));  // open: out_debug
  assign out = en_out ? out4_d : 4'bz;  // Controlled_Buffer controlled_buffer_1

  // Other names for the same wires on the sheet: bit0 = In_4[0]; bit1 = In_4[1]; bit2 = In_4[2]; bit3 = In_4[3]

  // Notes on the sheet:
  //   3a) Registro de Salida Restringida - 4 bits
  //   Nro de Grupo: 28
endmodule

module _3b_ALU_Reg_4bits (
  input  clk,
  input  [3:0] A,
  input  Write_A,
  input  [3:0] B,
  input  Write_B,
  input  [1:0] OP,
  input  en_out,
  output [3:0] A_debug,
  output [3:0] B_debug,
  output V,
  output N,
  output Z,
  output C,
  output [3:0] S_debug,
  output [3:0] S
);

  wire not_1_out;
  wire [3:0] alu_1_p8, n3a_reg_salida_restringida_4bits_1_out, n3a_reg_salida_restringida_4bits_2_out;

  Hex_Digit_Display hex_digit_display_1 (.value(A_debug));  // open: dp
  _3a_Reg_Salida_Restringida_4bits u_3a_reg_salida_restringida_4bits_1 (
    .In_4(A), .clk(clk), .out4_d(A_debug), .out(n3a_reg_salida_restringida_4bits_1_out), .w(Write_A),
    .en_out(1'b1));
  _3a_Reg_Salida_Restringida_4bits u_3a_reg_salida_restringida_4bits_2 (
    .In_4(B), .clk(clk), .out4_d(B_debug), .out(n3a_reg_salida_restringida_4bits_2_out), .w(Write_B),
    .en_out(1'b1));
  Hex_Digit_Display hex_digit_display_2 (.value(B_debug));  // open: dp
  // ALU alu_1: pin names not known; wires that end beside it: n3a_reg_salida_restringida_4bits_1_out, n3a_reg_salida_restringida_4bits_2_out, OP, V, N, Z, C, alu_1_p8
  not not_1 (not_1_out, clk);
  _3a_Reg_Salida_Restringida_4bits u_3a_reg_salida_restringida_4bits_3 (
    .In_4(alu_1_p8), .clk(not_1_out), .out4_d(S_debug), .out(S), .w(1'b1), .en_out(en_out));
  Hex_Digit_Display hex_digit_display_3 (.value(S_debug));  // open: dp

  // Notes on the sheet:
  //   3b) ALU con registros de entrada y salida - 4 bits
  //   Nro de Grupo: 28
  //   Completar con
  //   ALU del
  //   taller 1
endmodule

module _3c_Operacion_ALU_Reg_Bus_4bits (
  input  clk,
  input  w_alu_A,
  input  w_alu_B,
  input  [1:0] op,
  input  en_out_ALU,
  input  W_0,
  input  en_out_0,
  input  W_1,
  input  en_out_1,
  input  W_2,
  input  en_out_2,
  input  W_3,
  input  en_out_3,
  input  [3:0] Force_input,
  input  en_force_input,
  output V,
  output N,
  output V_2,
  output C
);

  wire [3:0] controlled_buffer_1_out, n3a_reg_salida_restringida_4bits_1_out,
       n3a_reg_salida_restringida_4bits_1_out4_d, n3a_reg_salida_restringida_4bits_2_out4_d,
       n3a_reg_salida_restringida_4bits_3_out4_d, n3a_reg_salida_restringida_4bits_4_out4_d,
       n3b_alu_reg_4bits_1_a_debug, n3b_alu_reg_4bits_1_b_debug, n3b_alu_reg_4bits_1_s_debug;

  assign controlled_buffer_1_out = en_force_input ? Force_input : 4'bz;  // Controlled_Buffer controlled_buffer_1
  _3a_Reg_Salida_Restringida_4bits u_3a_reg_salida_restringida_4bits_1 (
    .In_4(controlled_buffer_1_out), .clk(clk), .out4_d(n3a_reg_salida_restringida_4bits_1_out4_d),
    .out(n3a_reg_salida_restringida_4bits_1_out), .w(W_0), .en_out(en_out_0));
  _3a_Reg_Salida_Restringida_4bits u_3a_reg_salida_restringida_4bits_2 (
    .In_4(controlled_buffer_1_out), .clk(clk), .out4_d(n3a_reg_salida_restringida_4bits_2_out4_d),
    .out(n3a_reg_salida_restringida_4bits_1_out), .w(W_1), .en_out(en_out_1));
  _3a_Reg_Salida_Restringida_4bits u_3a_reg_salida_restringida_4bits_3 (
    .In_4(controlled_buffer_1_out), .clk(clk), .out4_d(n3a_reg_salida_restringida_4bits_3_out4_d),
    .out(n3a_reg_salida_restringida_4bits_1_out), .w(W_2), .en_out(en_out_2));
  _3a_Reg_Salida_Restringida_4bits u_3a_reg_salida_restringida_4bits_4 (
    .In_4(controlled_buffer_1_out), .clk(clk), .out4_d(n3a_reg_salida_restringida_4bits_4_out4_d),
    .out(n3a_reg_salida_restringida_4bits_1_out), .w(W_3), .en_out(en_out_3));
  Hex_Digit_Display hex_digit_display_1 (.value(n3a_reg_salida_restringida_4bits_1_out4_d));  // open: dp
  Hex_Digit_Display hex_digit_display_2 (.value(n3a_reg_salida_restringida_4bits_2_out4_d));  // open: dp
  Hex_Digit_Display hex_digit_display_3 (.value(n3a_reg_salida_restringida_4bits_3_out4_d));  // open: dp
  Hex_Digit_Display hex_digit_display_4 (.value(n3a_reg_salida_restringida_4bits_4_out4_d));  // open: dp
  Hex_Digit_Display hex_digit_display_5 (.value(n3a_reg_salida_restringida_4bits_1_out));  // open: dp
  Hex_Digit_Display hex_digit_display_6 (.value(n3b_alu_reg_4bits_1_a_debug));  // open: dp
  Hex_Digit_Display hex_digit_display_7 (.value(n3b_alu_reg_4bits_1_b_debug));  // open: dp
  Hex_Digit_Display hex_digit_display_8 (.value(n3b_alu_reg_4bits_1_s_debug));  // open: dp
  _3b_ALU_Reg_4bits u_3b_alu_reg_4bits_1 (
    .clk(clk), .A(n3a_reg_salida_restringida_4bits_1_out), .Write_A(w_alu_A),
    .B(n3a_reg_salida_restringida_4bits_1_out), .Write_B(w_alu_B), .OP(op),
    .A_debug(n3b_alu_reg_4bits_1_a_debug), .B_debug(n3b_alu_reg_4bits_1_b_debug),
    .S_debug(n3b_alu_reg_4bits_1_s_debug), .en_out(en_out_ALU), .V(V), .N(N), .Z(V_2), .C(C),
    .S(controlled_buffer_1_out));
  Hex_Digit_Display hex_digit_display_9 (.value(controlled_buffer_1_out));  // open: dp

  // Notes on the sheet:
  //   3c) Secuencia de Operacion ALU con registros y buses - 4 bits
  //   Nro de Grupo: 28
  //   Bus 1
  //   op
  //   =
  //   Bus 2
endmodule
